# Fritzing sketch DiceRollerSchematic (saved by Fritzing 0.9.4)
breadboards: 1

parts:
  Part1 = Arduino Uno (Rev3)
  LED1 = LED - 5mm [color="Red (633nm)" package="5 mm [THT]"]
  LED2 = smd LED [color="Red (633nm)" package="1206 [SMD]"]
  LED3 = smd LED [color="Red (633nm)" package="1206 [SMD]"]
  LED4 = smd LED [color="Red (633nm)" package="1206 [SMD]"]
  LED5 = smd LED [color="Red (633nm)" package="1206 [SMD]"]
  LED6 = smd LED [color="Red (633nm)" package="1206 [SMD]"]
  S1 = Pushbutton [package="[SMD]"]
  R1 = Resistor [tolerance=±5% resistance=220 package="0805 [SMD]"]
  R2 = Resistor [tolerance=±5% resistance=220 package="0805 [SMD]"]
  R3 = Resistor [tolerance=±5% resistance=220 package="0805 [SMD]"]
  R4 = Resistor [tolerance=±5% resistance=220 package="0805 [SMD]"]
  R5 = Resistor [tolerance=±5% resistance=220 package="0805 [SMD]"]
  R6 = Resistor [tolerance=±5% resistance=220 package="0805 [SMD]"]
  R7 = Resistor [tolerance=±5% resistance=220 package="0805 [SMD]"]

nets:
  N1: Part1.D8, LED3.anode
  N2: Part1.D11_PWM/MOSI, LED4.anode
  N3: Part1.D12/MISO, LED5.anode
  N4: Part1.D13/SCK, LED6.anode
  N5: Part1.D2, S1.Pin_1, S1.Pin_2, R7.Pin_0
  N6: Part1.D4, LED1.anode
  N7: Part1.D7, LED2.anode
  N8: Part1.5V, S1.Pin_3, S1.Pin_4
  N9: Part1.GND, R1.Pin_1, R2.Pin_1, R3.Pin_1, R4.Pin_1, R5.Pin_1, R6.Pin_1, R7.Pin_1
  N10: LED1.cathode, R6.Pin_0
  N11: LED2.cathode, R1.Pin_0
  N12: LED3.cathode, R5.Pin_0
  N13: LED4.cathode, R3.Pin_0
  N14: LED5.cathode, R2.Pin_0
  N15: LED6.cathode, R4.Pin_0
