# Fritzing sketch ProximitySensorSchematic (saved by Fritzing 0.9.4)
breadboards: 1

parts:
  Part1 = Arduino Uno (Rev3)
  HC-SR04_Sensor_1 = HC-SR04 Ultrasonic Distance Sensor
  LED1 = smd LED [color="Red (633nm)" package="0805 [SMD]"]
  R1 = Resistor [tolerance=±5% resistance=220 package="1206 [SMD]"]

nets:
  N1: Part1.D9_PWM, HC-SR04_Sensor_1.ECHO
  N2: Part1.D10_PWM/SS, HC-SR04_Sensor_1.TRIG
  N3: Part1.D2, LED1.anode
  5V: Part1.5V, HC-SR04_Sensor_1.VCC
  GND: Part1.GND, HC-SR04_Sensor_1.GND, R1.Pin_1
  N4: LED1.cathode, R1.Pin_0
